// Logisim project regfile.circ as structural Verilog: 2 circuits, main circuit main
module main (
  input  [4:0] Reg1_num,
  input  [4:0] Reg2,
  input  [4:0] Write_Reg_num,
  input  [31:0] Din,
  input  Write_Enable,
  input  Clock,
  output [31:0] Reg1,
  output [31:0] s0_Value,
  output [31:0] s1_Value,
  output [31:0] s2_Value,
  output [31:0] ra_Value,
  output [31:0] Reg2_2
);

  Multiplexer #(.width(32), .enable("false")) multiplexer_1 ();  // open: in0, in1, out, sel
  Register #(.width(32)) _0__Zero ();  // open: D, en, Q, clk, clr
  Register #(.width(32)) _8__t0 ();  // open: D, en, Q, clk, clr
  Register #(.width(32)) _16__s0 ();  // open: D, en, Q, clk, clr
  Register #(.width(32)) _24__t8 ();  // open: D, en, Q, clk, clr
  Register #(.width(32)) _1__at ();  // open: D, en, Q, clk, clr
  Register #(.width(32)) _9__t1 ();  // open: D, en, Q, clk, clr
  Register #(.width(32)) _17__s1 ();  // open: D, en, Q, clk, clr
  Register #(.width(32)) _25__t9 ();  // open: D, en, Q, clk, clr
  Register #(.width(32)) _2__v0 ();  // open: D, en, Q, clk, clr
  Register #(.width(32)) _10__t2 ();  // open: D, en, Q, clk, clr
  Register #(.width(32)) _18__s2 ();  // open: D, en, Q, clk, clr
  Register #(.width(32)) _26__k0 ();  // open: D, en, Q, clk, clr
  Register #(.width(32)) _3__v1 ();  // open: D, en, Q, clk, clr
  Register #(.width(32)) _11__t3 ();  // open: D, en, Q, clk, clr
  Register #(.width(32)) _19__s3 ();  // open: D, en, Q, clk, clr
  Register #(.width(32)) _27__k1 ();  // open: D, en, Q, clk, clr
  Register #(.width(32)) _4__a0 ();  // open: D, en, Q, clk, clr
  Register #(.width(32)) _12__t4 ();  // open: D, en, Q, clk, clr
  Register #(.width(32)) _20__s4 ();  // open: D, en, Q, clk, clr
  Register #(.width(32)) _28__gp ();  // open: D, en, Q, clk, clr
  Register #(.width(32)) _5__a1 ();  // open: D, en, Q, clk, clr
  Register #(.width(32)) _13__t5 ();  // open: D, en, Q, clk, clr
  Register #(.width(32)) _21__s5 ();  // open: D, en, Q, clk, clr
  Register #(.width(32)) _29__sp ();  // open: D, en, Q, clk, clr
  Register #(.width(32)) _6__a2 ();  // open: D, en, Q, clk, clr
  Register #(.width(32)) _14__t6 ();  // open: D, en, Q, clk, clr
  Register #(.width(32)) _22__s6 ();  // open: D, en, Q, clk, clr
  Register #(.width(32)) _30__fp ();  // open: D, en, Q, clk, clr
  Register #(.width(32)) _7__a3 ();  // open: D, en, Q, clk, clr
  Register #(.width(32)) _15__t7 ();  // open: D, en, Q, clk, clr
  Register #(.width(32)) _23__s7 ();  // open: D, en, Q, clk, clr
  Register #(.width(32)) _31__ra ();  // open: D, en, Q, clk, clr

  // Other names for the same wires on the sheet: clk = Clock; ra[31:0] = ra_Value; reg2_num[4:0] = Reg2;
  //   reg2_t[31:0] = Reg2_2; s0[31:0] = s0_Value; s1[31:0] = s1_Value; s2[31:0] = s2_Value; WE = Write_Enable;
  //   write_data[31:0] = Din

  // Notes on the sheet:
  //   输入引脚
  //   输出引脚
  //   Debug引脚，便于观测寄存器值
  //   请勿修改引脚以及封装，直接使用隧道连接电路
endmodule

module test (
);

  wire undriven;

  main main_1 (.Clock(undriven));  // open: Reg1_num, Reg2, Write_Reg_num, Din, Write_Enable, Reg1, Reg2_2, s0_Value, s1_Value, s2_Value, ra_Value
endmodule
